// Logisim project RAIYAN_MASOOD_HRIDDHO_1931117042_ASSIGNMENT_NO_04_CSE_332_LAB_SECTION_NO_01_SUMMER_2023_SEMESTER.circ as structural Verilog: 2 circuits, main circuit main
module main (
  input  [31:0] A,
  input  [31:0] B,
  input  [2:0] S,
  output Z,
  output [31:0] Y
);

  wire [31:0] adder_1_out, adder_2_out, and_1_out, comparator_1_gt, comparator_1_lt, shifter_1_out,
       shifter_2_out, subtractor_1_out;

  Adder #(.width(32)) adder_1 (.a(A), .b(B), .out(adder_1_out));  // open: cin, cout
  Subtractor #(.width(32)) subtractor_1 (.a(A), .b(B), .out(subtractor_1_out));  // open: bin, bout
  assign and_1_out = B & A;  // AND_Gate and_1, 32 bits wide
  Adder #(.width(32)) adder_2 (.a(A), .b(32'h1), .out(adder_2_out));  // open: cin, cout
  Shifter #(.width(32)) shifter_1 (.in(A), .\dist (B[4:0]), .out(shifter_1_out));
  Shifter #(.shift("ar"), .width(32)) shifter_2 (.in(A), .\dist (B[4:0]), .out(shifter_2_out));
  Comparator #(.width(32)) comparator_1 (
    .a(subtractor_1_out), .b({32{1'b0}}), .gt(comparator_1_gt[0]), .lt(comparator_1_lt[0]));  // open: eq
  Multiplexer #(.select(3), .width(32)) multiplexer_1 (
    .in0(adder_1_out), .in1(subtractor_1_out), .in2(and_1_out), .in3(adder_2_out), .in4(shifter_1_out),
    .in5(shifter_2_out), .in6(comparator_1_gt), .in7(comparator_1_lt), .out(Y), .sel(S));
  Comparator #(.width(32)) comparator_2 (.a({32{1'b0}}), .b(Y), .eq(Z));  // open: gt, lt
endmodule

module IC (
  input  [31:0] in_1,
  input  [31:0] in_2,
  input  [2:0] in_3,
  output out_4,
  output [31:0] out_5
);

  main main_1 (.A(in_1), .B(in_2), .S(in_3), .Z(out_4), .Y(out_5));
endmodule
